# Fritzing sketch IN_R_screenCpu (saved by Fritzing 0.9.3b)

parts:
  Raspberry_PI_4B+ = Raspberry Pi 4B
  Voice_Bonnet = Adafruit Voice Bonnet [part_number="Adafruit #4757"]
  Raspberry_pi_7'_Display_V1_1 = 3.5in tft touch screen
  Ribbon_TFT = Header 5x2 [package=2x5-shrouded_smd]
  SP1 = SPEAKER [package=pcb_mount_speaker]

nets:
  3V3: Raspberry_PI_4B+.3V3, Voice_Bonnet.3.3V
  N1: Raspberry_PI_4B+.5V, Voice_Bonnet.5.0V
  N2: Raspberry_PI_4B+.GPIO2, Voice_Bonnet.SDA
  N3: Raspberry_PI_4B+.GPIO3, Voice_Bonnet.SCL
  GND: Raspberry_PI_4B+.GND, Voice_Bonnet.GND, Raspberry_pi_7'_Display_V1_1.LCD_RD, Ribbon_TFT.10
  N4: Raspberry_PI_4B+.GPIO4, Voice_Bonnet.GPIO4
  N5: Raspberry_PI_4B+.GPIO14, Voice_Bonnet.TXD
  N6: Raspberry_PI_4B+.GPIO15, Voice_Bonnet.RXD
  N7: Raspberry_PI_4B+.GPIO17, Voice_Bonnet.BUTTON
  N8: Raspberry_PI_4B+.GPIO18, Voice_Bonnet.I2S_BCLK
  N9: Raspberry_PI_4B+.GPIO27, Voice_Bonnet.GPIO27
  N10: Raspberry_PI_4B+.GPIO22, Voice_Bonnet.GPIO22
  N11: Raspberry_PI_4B+.GPIO23, Voice_Bonnet.GPIO23
  N12: Raspberry_PI_4B+.GPIO24, Voice_Bonnet.GPIO24
  N13: Raspberry_PI_4B+.GPIO10, Voice_Bonnet.MOSI
  N14: Raspberry_PI_4B+.GPIO9, Voice_Bonnet.MISO
  N15: Raspberry_PI_4B+.GPIO25, Voice_Bonnet.GPIO25
  N16: Raspberry_PI_4B+.GPIO11, Voice_Bonnet.SCLK
  N17: Raspberry_PI_4B+.GPIO8, Voice_Bonnet.CE0
  N18: Raspberry_PI_4B+.GPIO7, Voice_Bonnet.CE1
  N19: Raspberry_PI_4B+.ID_SD, Voice_Bonnet.EED
  N20: Raspberry_PI_4B+.ID_SC, Voice_Bonnet.EEC
  N21: Raspberry_PI_4B+.GPIO5, Voice_Bonnet.LEDD
  N22: Raspberry_PI_4B+.GPIO6, Voice_Bonnet.LEDC
  N23: Raspberry_PI_4B+.GPIO12, Voice_Bonnet.PWM0
  N24: Raspberry_PI_4B+.GPIO13, Voice_Bonnet.GPIO13
  N25: Raspberry_PI_4B+.GPIO19, Voice_Bonnet.I2S_LRCLK
  N26: Raspberry_PI_4B+.GPIO16, Voice_Bonnet.GPIO19
  N27: Raspberry_PI_4B+.GPIO26, Voice_Bonnet.GPIO26
  N28: Raspberry_PI_4B+.GPIO20, Voice_Bonnet.I2S_DIN
  N29: Raspberry_PI_4B+.GPIO21, Voice_Bonnet.I2S_DOUT
  N30: Voice_Bonnet.RIGHT_P, SP1.+
  N31: Voice_Bonnet.RIGHT_N, SP1.-
  N32: Raspberry_pi_7'_Display_V1_1.VCC, Ribbon_TFT.2
  N33: Raspberry_pi_7'_Display_V1_1.NC, Ribbon_TFT.4
  N34: Raspberry_pi_7'_Display_V1_1.LCD_RS, Ribbon_TFT.6
  N35: Raspberry_pi_7'_Display_V1_1.LCD_WR, Ribbon_TFT.8

custom parts:
  Adafruit Voice Bonnet: Your Raspberry Pi computer is like an electronic brain - and with the Adafruit Voice Bonnet you can give it a mouth and ears as well! Featuring two microphones and two 1 Watt speaker outputs using a high quality I2S codec, this Pi add-on will work with any Raspberry Pi with a 2x20 connector - from the Pi Zero up to the Pi 4 and beyond (basically all but the very first ones made). The on-board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
  3.5in tft touch screen: 3.2" tft touch screen lcd display
