# Fritzing sketch IN_L_AnlgIface (saved by Fritzing 0.9.3b)
breadboards: 1

parts:
  M1 = DOIT Esp32 DevKit v1 (30 pins long, 11 pins width) [part_number=ESP32S-PIN30]
  0_7'_dual_LCD_screen = Waveshare 1.28 inch Round 240x240 LCD Display
  LCD2 = Waveshare 1.28 inch Round 240x240 LCD Display
  U2 = WS2812 RGB LED strip
  WS2812B = WS2812 RGB LED strip
  S1 = SWITCH-MOMENTARY-2 [package=tactile_switch_tall]
  S2 = SWITCH-MOMENTARY-2 [package=tactile_switch_tall]
  S3 = SWITCH-MOMENTARY-2 [package=tactile_switch_tall]
  S4 = SWITCH-MOMENTARY-2 [package=tactile_switch_tall]
  S5 = Round Pushbutton
  S6 = Round Pushbutton
  U4 = POT [package=pot_mammoth]

nets:
  N1: M1.3V3, 0_7'_dual_LCD_screen.pin_1, LCD2.pin_1
  N2: M1.GND, 0_7'_dual_LCD_screen.pin2, LCD2.pin2, WS2812B.GND#4, S1.1, S2.1, S3.1, S4.1, U4.E
  N3: M1.D2, 0_7'_dual_LCD_screen.pin_5
  N4: M1.D4, U4.A
  N5: M1.D5, LCD2.pin_5
  N6: M1.D18, 0_7'_dual_LCD_screen.pin4, LCD2.pin4
  N7: M1.D21, 0_7'_dual_LCD_screen.pin_7
  N8: M1.D23, 0_7'_dual_LCD_screen.pin3, LCD2.pin3
  N9: M1.D34, S4.2
  N10: M1.D35, S3.2
  N11: M1.D32, S2.2
  N12: M1.D33, S1.2
  N13: M1.D25, WS2812B.DOUT
  N14: M1.D26, 0_7'_dual_LCD_screen.pin_6, LCD2.pin_6
  N15: M1.D27, LCD2.pin_7
  N16: M1.D14, S5.leg1
  N17: M1.D12, S6.leg1
  N18: M1.VIN, 0_7'_dual_LCD_screen.pin_8, LCD2.pin_8, WS2812B.VCC#5, U4.S
  N19: U2.GND, WS2812B.GND#0
  N20: U2.VCC, WS2812B.VCC#1
  N21: U2.DOUT, WS2812B.DIN
  N22: S5.leg0, S6.leg0

custom parts:
  DOIT Esp32 DevKit v1 (30 pins long, 11 pins width): The DOIT Esp32 DevKit v1 is one of the development board created by DOIT to evaluate the ESP-WROOM-32 module. It is based on the ESP32 microcontroller that boasts Wifi, Bluetooth, Ethernet and Low Power support all in a single chip. (vanepp) made breadboard work, adjusted pin numbering and labels and reduced size of schematic and cleaned up pcb. This chip is 30pins long (2 x15) and 11 pins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
  Waveshare 1.28 inch Round 240x240 LCD Display: Waveshare 1.28 inch Round 240x240 LCD Display with GC9A01 Controller
  WS2812 RGB LED strip: WS2812 strip
